# Fritzing sketch rpi_car (saved by Fritzing 0.8.7b)
breadboards: 1

parts:
  Raspberry_Pi_B_rev1 = Raspberry Pi B rev2
  J1 = Basic Servo
  J2 = Basic Servo
  BAT1 = Battery Holders [package=battery]
  Part1 = SRF05 Ultrasonic Rangefinder
  R1 = Resistor [tolerance=±5% resistance=1k package=THT]
  R2 = Resistor [tolerance=±5% resistance=1.5k package=THT]
  part = Basic Servo  # not connected
  U1 = L298_BRIDGE_DRIVER [package=powerso20]
  M1 = DC Motor
  U2 = LIPO-2000mAh [package=lipo-2000]

nets:
  5V: Raspberry_Pi_B_rev1.5V, Part1.VCC, U1.VS
  GND: Raspberry_Pi_B_rev1.GND, J1.gnd, J2.gnd, BAT1.-, Part1.GND, R2.Pin_1, U1.GND, U2.-
  N1: Raspberry_Pi_B_rev1.GPIO_23, J1.pulse
  N2: Raspberry_Pi_B_rev1.GPIO_17, U1.IN1
  N3: Raspberry_Pi_B_rev1.GPIO_18, J2.pulse
  N4: Raspberry_Pi_B_rev1.GPIO_27, U1.IN2
  N5: Raspberry_Pi_B_rev1.GPIO_22, R1.Pin_1, R2.Pin_0
  N6: Raspberry_Pi_B_rev1.GPIO_24, Part1.Trig
  N7: Raspberry_Pi_B_rev1.GPIO_25, U1.ENA
  VCC: J1.vcc, J2.vcc, BAT1.+
  N8: Part1.Echo, R1.Pin_0
  N9: U1.OUT1, M1.pin_1
  N10: U1.OUT2, M1.pin_2
  N11: U1.VSS, U2.+
